# Fritzing sketch RFID-and-NodeMCU (saved by Fritzing 0.9.5d)

parts:
  NodeMCU = ESP8266 NodeMCU LoLin base
  RFID = RFID-RC522-v2

nets:
  N1: NodeMCU.3V1-3, NodeMCU.3V3-2, NodeMCU.3V3-3, RFID.3.3V
  N2: NodeMCU.D1-0, NodeMCU.D1-3, RFID.RST
  N3: NodeMCU.D2-3, RFID.SDA
  N4: NodeMCU.D5-1, NodeMCU.D5-3, RFID.SCK
  N5: NodeMCU.D6-3, RFID.MISO
  N6: NodeMCU.D7-1, NodeMCU.D7-3, RFID.MOSI
  N7: NodeMCU.GND3-3, RFID.GND

custom parts:
  ESP8266 NodeMCU LoLin base: ESP8266 based NodeMCU Base
  RFID-RC522-v2: A simple China made RFID-RC522 Reader; do check the pin labels, as this is a MFRC522 based clone.
